# Fritzing sketch Wiring-Lengkap (saved by Fritzing 0.9.5d)

parts:
  CPU1 = NodeMCU WROOM ESP 32
  U1 = DFRobot SEN0189 [package=THT]
  S1 = PH meter [package=THT]  # not connected
  M1 = ph-4502c [package=THT]  # not connected
  A1 = tds-sensor-meter-v1.0_1
  U2 = Turbidity Sensor Probe [package=THT]

nets:
  N1: CPU1.pin_15, U1.P1_3
  N2: CPU1.pin_16, U1.P1_2
  N3: CPU1.pin_17, A1.pin2
  N4: CPU1.pin_18, A1.pin3
  N5: U1.P2_1, U2.pin1
  N6: U1.P2_2, U2.VCC
  N7: U1.P2_3, U2.pin2

custom parts:
  NodeMCU WROOM ESP 32: 30 pol Development Kit
  DFRobot SEN0189: Turbidity sensor of DFRobot SEN0189
  ph-4502c: ph-4502c PH Meter.
  : TDS Meter V1.0 Development Board Water Meter Filter Measuring Water Sensor Module.
  Turbidity Sensor Probe: Turbidity sensor probe to the DFRobot measure module.
